# Fritzing sketch BinaryCounter (saved by Fritzing 0.9.3b)
circuit board: 8.46667cm x 5.64444cm
breadboards: 1

parts:
  Binary_Counter = Arduino Uno (Rev3)
  LED1 = LED - 5mm [color="Red (633nm)" package="5 mm [THT]"]
  R2 = Resistor [tolerance=±5% resistance=330 package=THT]
  R3 = Resistor [tolerance=±5% resistance=330 package=THT]
  R4 = Resistor [tolerance=±5% resistance=330 package=THT]
  LED2 = LED - 5mm [color="Red (633nm)" package="5 mm [THT]"]
  LED3 = LED - 5mm [color="Red (633nm)" package="5 mm [THT]"]
  LED4 = LED - 5mm [color="Red (633nm)" package="5 mm [THT]"]
  R1 = Resistor [tolerance=±5% resistance=330 package=THT]

nets:
  N1: Binary_Counter.GND, LED1.cathode, LED2.cathode, LED3.cathode, LED4.cathode
  N2: Binary_Counter.D2, R1.Pin_0
  N3: Binary_Counter.D3_PWM, R2.Pin_0
  N4: Binary_Counter.D4, R3.Pin_0
  N5: Binary_Counter.D5_PWM, R4.Pin_0
  N6: LED1.anode, R1.Pin_1
  N7: R2.Pin_1, LED2.anode
  N8: R3.Pin_1, LED3.anode
  N9: R4.Pin_1, LED4.anode
