# Fritzing sketch DebugAnalogInput (saved by Fritzing 0.9.3b)
breadboards: 1

parts:
  Debug_Analog_Input = Arduino Uno (Rev3)
  R1 = Trimmer Potentiometer [maximum_resistance=10kΩ package=THT]

nets:
  N1: Debug_Analog_Input.A0, R1.wiper
  N2: Debug_Analog_Input.D9_PWM, R1.leg2
  N3: Debug_Analog_Input.GND, R1.leg1
