# Fritzing sketch SerialInput (saved by Fritzing 0.9.3b)
breadboards: 1

parts:
  Serial_Input = Arduino Uno (Rev3)
  LED1 = LED - 5mm [color="Red (633nm)" package="5 mm [THT]"]
  R1 = Resistor [tolerance=±5% resistance=330 package=THT]

nets:
  N1: Serial_Input.GND, LED1.cathode
  N2: Serial_Input.D7, R1.Pin_1
  N3: LED1.anode, R1.Pin_0
